// Logisim project CPU.circ as structural Verilog: 6 circuits, main circuit main
module main (
  input  [31:0] in_1
);

  wire alu_1_zero, and_1_out, clock_1_out, control_unit_1_alu_op__0, control_unit_1_alu_op__1,
       control_unit_1_alu_op__2, control_unit_1_alusrc, control_unit_1_branch, control_unit_1_memtoreg,
       control_unit_1_memwrite, control_unit_1_regdst, control_unit_1_regwrite;
  wire [2:0] alu_control_1_output;
  wire [3:0] multiplexer_1_out;
  wire [31:0] adder_1_out, adder_2_out, alu_1_output, bit_extender_1_out, multiplexer_2_out,
       multiplexer_4_out, pc_q, ram_1_data, ram_2_data, register_file_1_read_data_1,
       register_file_1_read_data_2, shifter_1_out;

  Register #(.width(32)) pc (.D(in_1), .en(1'b1), .Q(pc_q), .clk(clock_1_out));  // open: clr
  RAM #(.addrWidth(24), .dataWidth(32)) ram_1 (
    .addr(pc_q[23:0]), .data(ram_1_data), .sel(1'b1), .clk(clock_1_out), .ld(1'b1));  // open: clr
  Control_Unit control_unit_1 (
    .OP3(ram_1_data[31]), .OP2(ram_1_data[30]), .OP1(ram_1_data[29]), .RegDst(control_unit_1_regdst),
    .ALUSrc(control_unit_1_alusrc), .MemToReg(control_unit_1_memtoreg), .RegWrite(control_unit_1_regwrite),
    .MemWrite(control_unit_1_memwrite), .Branch(control_unit_1_branch), .ALU_OP__2(control_unit_1_alu_op__2),
    .ALU_OP__1(control_unit_1_alu_op__1), .ALU_OP__0(control_unit_1_alu_op__0));
  Clock clock_1 (.out(clock_1_out));
  Multiplexer #(.width(4), .enable("false")) multiplexer_1 (
    .in0(ram_1_data[24:21]), .in1(ram_1_data[20:17]), .out(multiplexer_1_out), .sel(control_unit_1_regdst));
  Register_File register_file_1 (
    .Read_Addr_1(ram_1_data[28:25]), .Read_Addr_2(ram_1_data[24:21]), .Write_Addr(multiplexer_1_out),
    .Write_Data(multiplexer_4_out), .Reg_Write(control_unit_1_regwrite), .clk(clock_1_out),
    .Read_Data_1(register_file_1_read_data_1), .Read_Data_2(register_file_1_read_data_2));
  assign bit_extender_1_out = {{11{1'b0}}, ram_1_data[20:0]};  // Bit_Extender bit_extender_1
  Adder #(.width(32)) adder_1 (.a(32'h4), .b(pc_q), .out(adder_1_out));  // open: cin, cout
  Shifter #(.width(32)) shifter_1 (.in(bit_extender_1_out), .\dist (5'b00010), .out(shifter_1_out));
  ALU alu_1 (
    .input_1(register_file_1_read_data_1), .input_2(multiplexer_2_out), .Zero(alu_1_zero),
    .ALU_Ctr(alu_control_1_output), .\output (alu_1_output));
  Multiplexer #(.width(32), .enable("false")) multiplexer_2 (
    .in0(register_file_1_read_data_2), .in1(bit_extender_1_out), .out(multiplexer_2_out),
    .sel(control_unit_1_alusrc));
  ALU_Control alu_control_1 (
    .Function(ram_1_data[2:0]), .OP3(control_unit_1_alu_op__2), .OP2(control_unit_1_alu_op__1),
    .OP1(control_unit_1_alu_op__0), .\output (alu_control_1_output));
  Adder #(.width(32)) adder_2 (.a(adder_1_out), .b(shifter_1_out), .out(adder_2_out));  // open: cin, cout
  and and_1 (and_1_out, control_unit_1_branch, ~alu_1_zero);  // AND_Gate
  Multiplexer #(.width(32), .enable("false")) multiplexer_3 (
    .in0(adder_1_out), .in1(adder_2_out), .out(in_1), .sel(and_1_out));
  RAM #(.addrWidth(24), .dataWidth(32), .bus("separate")) ram_2 (
    .addr(alu_1_output[23:0]), .din(register_file_1_read_data_2), .data(ram_2_data),
    .str(control_unit_1_memwrite), .sel(1'b1), .clk(clock_1_out), .ld(1'b1));  // open: clr
  Multiplexer #(.width(32), .enable("false")) multiplexer_4 (
    .in0(ram_2_data), .in1(alu_1_output), .out(multiplexer_4_out), .sel(control_unit_1_memtoreg));
endmodule

// Reg File
module Register_File (
  input  Reg_Write,
  input  [3:0] Read_Addr_1,
  input  [3:0] Read_Addr_2,
  input  [3:0] Write_Addr,
  input  [31:0] Write_Data,
  input  clk,
  output [31:0] Read_Data_1,
  output [31:0] Read_Data_2
);

  wire [31:0] a1_q, a2_q, a3_q, at_q, demultiplexer_1_out0, demultiplexer_1_out1, demultiplexer_1_out2,
       demultiplexer_1_out3, demultiplexer_1_out4, demultiplexer_1_out5, demultiplexer_1_out6,
       demultiplexer_1_out7, demultiplexer_1_out8, demultiplexer_1_out9, demultiplexer_1_out10,
       demultiplexer_1_out11, demultiplexer_1_out12, demultiplexer_1_out13, demultiplexer_1_out14,
       demultiplexer_1_out15, l1_q, l2_q, l3_q, t1_q, t2_q, t3_q, t4_q, t5_q, t6_q, t7_q, t8_q, zero_q;

  Demultiplexer #(.select(4), .width(32)) demultiplexer_1 (
    .out0(demultiplexer_1_out0), .out1(demultiplexer_1_out1), .out2(demultiplexer_1_out2),
    .out3(demultiplexer_1_out3), .out4(demultiplexer_1_out4), .out5(demultiplexer_1_out5),
    .out6(demultiplexer_1_out6), .out7(demultiplexer_1_out7), .out8(demultiplexer_1_out8),
    .out9(demultiplexer_1_out9), .out10(demultiplexer_1_out10), .out11(demultiplexer_1_out11),
    .out12(demultiplexer_1_out12), .out13(demultiplexer_1_out13), .out14(demultiplexer_1_out14),
    .out15(demultiplexer_1_out15), .in(Write_Data), .sel(Write_Addr), .en(Reg_Write));
  Register #(.width(32)) at (.D(demultiplexer_1_out1), .en(1'b1), .Q(at_q), .clk(clk));  // open: clr
  Register #(.width(32)) a2 (.D(demultiplexer_1_out3), .en(1'b1), .Q(a2_q), .clk(clk));  // open: clr
  Register #(.width(32)) l1 (.D(demultiplexer_1_out5), .en(1'b1), .Q(l1_q), .clk(clk));  // open: clr
  Register #(.width(32)) l3 (.D(demultiplexer_1_out7), .en(1'b1), .Q(l3_q), .clk(clk));  // open: clr
  Register #(.width(32)) t2 (.D(demultiplexer_1_out9), .en(1'b1), .Q(t2_q), .clk(clk));  // open: clr
  Register #(.width(32)) t4 (.D(demultiplexer_1_out11), .en(1'b1), .Q(t4_q), .clk(clk));  // open: clr
  Register #(.width(32)) t6 (.D(demultiplexer_1_out13), .en(1'b1), .Q(t6_q), .clk(clk));  // open: clr
  Register #(.width(32)) t8 (.D(demultiplexer_1_out15), .en(1'b1), .Q(t8_q), .clk(clk));  // open: clr
  Register #(.width(32)) zero (.D(demultiplexer_1_out0), .en(1'b1), .Q(zero_q), .clk(clk));  // open: clr
  Register #(.width(32)) a1 (.D(demultiplexer_1_out2), .en(1'b1), .Q(a1_q), .clk(clk));  // open: clr
  Register #(.width(32)) a3 (.D(demultiplexer_1_out4), .en(1'b1), .Q(a3_q), .clk(clk));  // open: clr
  Register #(.width(32)) l2 (.D(demultiplexer_1_out6), .en(1'b1), .Q(l2_q), .clk(clk));  // open: clr
  Register #(.width(32)) t1 (.D(demultiplexer_1_out8), .en(1'b1), .Q(t1_q), .clk(clk));  // open: clr
  Register #(.width(32)) t3 (.D(demultiplexer_1_out10), .en(1'b1), .Q(t3_q), .clk(clk));  // open: clr
  Register #(.width(32)) t5 (.D(demultiplexer_1_out12), .en(1'b1), .Q(t5_q), .clk(clk));  // open: clr
  Register #(.width(32)) t7 (.D(demultiplexer_1_out14), .en(1'b1), .Q(t7_q), .clk(clk));  // open: clr
  Multiplexer #(.select(4), .width(32), .enable("false")) multiplexer_1 (
    .in0(zero_q), .in1(at_q), .in2(a1_q), .in3(a2_q), .in4(a3_q), .in5(l1_q), .in6(l2_q), .in7(l3_q),
    .in8(t1_q), .in9(t2_q), .in10(t3_q), .in11(t4_q), .in12(t5_q), .in13(t6_q), .in14(t7_q), .in15(t8_q),
    .out(Read_Data_1), .sel(Read_Addr_1));
  Multiplexer #(.select(4), .width(32), .enable("false")) multiplexer_2 (
    .in0(zero_q), .in1(at_q), .in2(a1_q), .in3(a2_q), .in4(a3_q), .in5(l1_q), .in6(l2_q), .in7(l3_q),
    .in8(t1_q), .in9(t2_q), .in10(t3_q), .in11(t4_q), .in12(t5_q), .in13(t6_q), .in14(t7_q), .in15(t8_q),
    .out(Read_Data_2), .sel(Read_Addr_2));

  // Notes on the sheet:
  //   Register File
endmodule

module Control_Unit (
  input  OP3,
  input  OP2,
  input  OP1,
  output RegDst,
  output ALUSrc,
  output MemToReg,
  output RegWrite,
  output MemWrite,
  output Branch,
  output ALU_OP__2,
  output ALU_OP__1,
  output ALU_OP__0
);

  wire and_5_out, and_6_out;

  and and_1 (RegDst, ~OP3, ~OP2, ~OP1);  // AND_Gate
  and and_2 (Branch, OP3, OP2, OP1);
  and and_3 (MemToReg, ~OP3, ~OP2, OP1);  // AND_Gate
  and and_4 (MemWrite, ~OP3, OP2, ~OP1);  // AND_Gate
  and and_5 (and_5_out, OP3, ~OP2, ~OP1);  // AND_Gate
  and and_6 (and_6_out, OP3, ~OP2, OP1);  // AND_Gate
  or or_1 (ALUSrc, and_6_out, and_5_out, MemWrite, MemToReg);
  or or_2 (RegWrite, and_6_out, and_5_out, MemToReg, RegDst);

  assign ALU_OP__0 = OP1;
  assign ALU_OP__1 = OP2;
  assign ALU_OP__2 = OP3;

  // Notes on the sheet:
  //   R-type
  //   bnq
  //   lw
  //   sw
  //   Control Unit
  //   andi
  //   ori
endmodule

module ALU (
  input  [31:0] input_1,
  input  [31:0] input_2,
  input  [2:0] ALU_Ctr,
  output Zero,
  output [31:0] \output 
);

  wire [31:0] adder_1_out, AND_out, multiplier_1_out, NAND_out, NOR_out, OR_out, subtractor_1_out;

  Comparator #(.width(32), .mode("unsigned")) comparator_1 (.a(input_1), .b(input_2), .eq(Zero));  // open: gt, lt
  Adder #(.width(32)) adder_1 (.a(input_1), .b(input_2), .out(adder_1_out));  // open: cin, cout
  Subtractor #(.width(32)) subtractor_1 (.a(input_1), .b(input_2), .out(subtractor_1_out));  // open: bin, bout
  Multiplier #(.width(32)) multiplier_1 (.a(input_1), .b(input_2), .out(multiplier_1_out));  // open: cin, cout
  assign AND_out = input_1 & input_2;  // AND_Gate AND, 32 bits wide
  assign OR_out = input_1 | input_2;  // OR_Gate OR, 32 bits wide
  assign NOR_out = ~(input_1 | input_2);  // NOR_Gate NOR, 32 bits wide
  assign NAND_out = ~(input_1 & input_2);  // NAND_Gate NAND, 32 bits wide
  Multiplexer #(.select(3), .width(32), .enable("false")) multiplexer_1 (
    .in0({32{1'b1}}), .in1(adder_1_out), .in2(subtractor_1_out), .in3(multiplier_1_out), .in4(AND_out),
    .in5(OR_out), .in6(NOR_out), .in7(NAND_out), .out(\output ), .sel(ALU_Ctr));

  // Notes on the sheet:
  //   ALU
endmodule

// SubCtrl
module ALU_SubControl (
  input  OP3,
  input  OP2,
  input  OP1,
  output [2:0] A
);

  wire andi_out, lw_out, ori_out, sw_out;

  and bnq (A[1], OP3, OP2, OP1);
  and lw (lw_out, ~OP3, ~OP2, OP1);  // AND_Gate
  and sw (sw_out, ~OP3, OP2, ~OP1);  // AND_Gate
  and andi (andi_out, OP3, ~OP2, ~OP1);  // AND_Gate
  and ori (ori_out, OP3, ~OP2, OP1);  // AND_Gate
  or or_1 (A[0], ori_out, andi_out);
  or or_2 (A[2], ori_out, sw_out, lw_out);

  // Notes on the sheet:
  //   ALU SubControl
endmodule

module ALU_Control (
  input  OP3,
  input  OP2,
  input  OP1,
  input  [2:0] Function,
  output [2:0] \output 
);

  wire [2:0] alu_subcontrol_1_a;

  ALU_SubControl alu_subcontrol_1 (.OP3(OP3), .OP2(OP2), .OP1(OP1), .A(alu_subcontrol_1_a));
  Multiplexer #(.width(3), .enable("false")) multiplexer_1 (
    .in0(alu_subcontrol_1_a), .in1(Function), .out(\output ));  // open: sel

  // Notes on the sheet:
  //   ALU Control
endmodule
